# Fritzing sketch rpi (saved by Fritzing 0.9.3b)
breadboards: 1

parts:
  Bauteil1 = Adafruit T-Cobbler Plus [part_number="Adafruit #1989 and #2028"]
  Bauteil2 = RFID-RC522-v2

nets:
  N1: Bauteil1.SDA, Bauteil2.3.3V
  N2: Bauteil1.GND, Bauteil2.SCK
  N3: Bauteil1.GPIO17, Bauteil2.GND
  N4: Bauteil1.MISO, Bauteil2.MOSI
  N5: Bauteil1.SCLK, Bauteil2.MISO
  N6: Bauteil1.CE0, Bauteil2.RST
  N7: Bauteil1.CE1, Bauteil2.SDA

custom parts:
  Adafruit T-Cobbler Plus: The Raspberry Pi has landed on the Maker World like a 40-GPIO pinned, quad-USB ported, credit card sized bomb of DIY joy. And while you can use most of our great Model B accessories by hooking up our downgrade cable, its probably a good time to upgrade your set up and accessorize using all of the 40 pins. That's why we now carry the Assembled Adafruit Pi T-Cobbler Plus - Breakout + Cable for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
  RFID-RC522-v2: A simple China made RFID-RC522 Reader; do check the pin labels, as this is a MFRC522 based clone.
