# Fritzing sketch picopi (saved by Fritzing 0.9.3b)
breadboards: 1

parts:
  Mod1 = Raspberry Pi Pico
  Bauteil1 = RFID-RC522-v2

nets:
  N1: Mod1.pin_1, Bauteil1.RST
  N2: Mod1.pin_2, Bauteil1.SDA
  N3: Mod1.pin_3, Mod1.pin_8, Mod1.pin_13, Mod1.pin_18, Mod1.pin_23, Mod1.pin_28, Mod1.pin_33, Mod1.pin_38, Bauteil1.GND
  N4: Mod1.pin_4, Bauteil1.SCK
  N5: Mod1.pin_5, Bauteil1.MOSI
  N6: Mod1.pin_6, Bauteil1.MISO
  N7: Mod1.pin_36, Bauteil1.3.3V

custom parts:
  Raspberry Pi Pico: Raspberry Pi Pico. Based around the RP2040 microcontroller the Pico is a low cost microcontroller device bringing Raspberry Pi quality, cost, and easy of use to the microcontroller space. Jan 2021, Split part in to two versions: tht (this one) and SMD. This one will drill holes for a .1 in header in pcb to allow plugging in the module as well as providing pads to solder the module to the top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
  RFID-RC522-v2: A simple China made RFID-RC522 Reader; do check the pin labels, as this is a MFRC522 based clone.
