# Fritzing sketch picopi (saved by Fritzing 0.9.3b)
breadboards: 1

parts:
  Mod1 = Raspberry Pi Pico
  R1 = Resistor [tolerance=±5% resistance=220 package=THT]
  R2 = Resistor [tolerance=±5% resistance=220 package=THT]
  R3 = Resistor [tolerance=±5% resistance=470 package=THT]
  R4 = Resistor [tolerance=±5% resistance=330 package=THT]
  LED2 = LED - 3mm [color="Blue (470nm)" package="3 mm [THT]"]
  LED1 = LED - 3mm [color="Red (633nm)" package="3 mm [THT]"]
  hc-sr1 = hc-sr04

nets:
  N1: Mod1.pin_3, Mod1.pin_8, Mod1.pin_13, Mod1.pin_18, Mod1.pin_23, Mod1.pin_28, Mod1.pin_33, Mod1.pin_38, R3.Pin_0, LED2.cathode, LED1.cathode, hc-sr1.GND
  N2: Mod1.pin_19, R2.Pin_1
  N3: Mod1.pin_20, R1.Pin_1
  N4: Mod1.pin_21, hc-sr1.Trig
  N5: Mod1.pin_22, R3.Pin_1, R4.Pin_0
  N6: Mod1.pin_40, hc-sr1.VCC
  N7: R1.Pin_0, LED1.anode
  N8: R2.Pin_0, LED2.anode
  N9: R4.Pin_1, hc-sr1.Echo

custom parts:
  Raspberry Pi Pico: Raspberry Pi Pico. Based around the RP2040 microcontroller the Pico is a low cost microcontroller device bringing Raspberry Pi quality, cost, and easy of use to the microcontroller space. Jan 2021, Split part in to two versions: tht (this one) and SMD. This one will drill holes for a .1 in header in pcb to allow plugging in the module as well as providing pads to solder the module to the top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
