# Fritzing sketch rpi (saved by Fritzing 0.9.3b)
breadboards: 1

parts:
  Bauteil1 = Adafruit T-Cobbler Plus [part_number="Adafruit #1989 and #2028"]
  hc-sr1 = hc-sr04
  LED1 = LED - 5mm [color="Red (633nm)" package="5 mm [THT]"]
  LED2 = LED - 5mm [color="Blue (430nm)" package="5 mm [THT]"]
  R1 = Resistor [tolerance=±5% resistance=220 package=THT]
  R2 = Resistor [tolerance=±5% resistance=220 package=THT]
  R3 = Resistor [tolerance=±5% resistance=470 package=THT]
  R4 = Resistor [tolerance=±5% resistance=330 package=THT]

nets:
  GND: Bauteil1.GND, hc-sr1.GND, LED1.cathode, LED2.cathode, R3.Pin_0
  N1: Bauteil1.GPIO5, R2.Pin_1
  N2: Bauteil1.GPIO26, R1.Pin_1
  +5V: Bauteil1.+5V, hc-sr1.VCC
  N3: Bauteil1.GPIO16, R3.Pin_1, R4.Pin_0
  N4: Bauteil1.GPIO21, hc-sr1.Trig
  N5: hc-sr1.Echo, R4.Pin_1
  N6: LED1.anode, R1.Pin_0
  N7: LED2.anode, R2.Pin_0

custom parts:
  Adafruit T-Cobbler Plus: The Raspberry Pi has landed on the Maker World like a 40-GPIO pinned, quad-USB ported, credit card sized bomb of DIY joy. And while you can use most of our great Model B accessories by hooking up our downgrade cable, its probably a good time to upgrade your set up and accessorize using all of the 40 pins. That's why we now carry the Assembled Adafruit Pi T-Cobbler Plus - Breakout + Cable for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
